// Logisim project Template.circ as structural Verilog: 6 circuits, main circuit main
module main (
  input  CLR,
  output [15:0] FETCH_OUT,
  output [14:0] PC_IN
);

  wire binst_1_op, button_1_out, clk, minst_1_op, or_1_out;
  wire [0:0] PC_q;
  wire [15:0] adder_1_out, binst_1_instru, calc_adr_1_adr_out, minst_1_instru, multiplexer_1_out,
       multiplexer_2_out, multiplexer_3_out, multiplexer_4_out;

  // Text text_1: pin names not known
  // Text text_2: pin names not known
  // Text text_3: pin names not known
  // Text text_4: pin names not known
  // Text text_5: pin names not known
  Adder #(.width(16)) adder_1 (.a({PC_IN, PC_q[0]}), .b(16'h2), .out(adder_1_out));  // open: cin, cout
  Multiplexer #(.width(16), .enable("false")) multiplexer_1 (
    .in0(adder_1_out), .in1(16'h30), .out(multiplexer_1_out), .sel(button_1_out));
  Button button_1 (.out(button_1_out));
  Clock #(.highDuration(4), .lowDuration(4)) u_clk (.out(clk));
  Clock sysclk ();  // open: out
  // Probe on calc_adr_1_adr_out
  CALC_ADR calc_adr_1 (.PC({PC_IN, PC_q[0]}), .ADR(multiplexer_4_out), .ADR_OUT(calc_adr_1_adr_out));
  Multiplexer #(.width(16), .enable("false")) multiplexer_2 (
    .in0(multiplexer_1_out), .in1(calc_adr_1_adr_out), .out(multiplexer_2_out), .sel(or_1_out));
  Register #(.width(16)) PC (.D(multiplexer_2_out), .en(1'b1), .clk(clk), .Q({PC_IN, PC_q[0]}), .clr(CLR));
  ROM #(.addrWidth(15), .dataWidth(16)) MEM_INSTRU (.addr(PC_IN), .data(FETCH_OUT));
  BINST binst_1 (.INST(FETCH_OUT), .INSTRU(binst_1_instru), .OP(binst_1_op));
  Multiplexer #(.width(16), .enable("false")) multiplexer_3 (
    .in0(binst_1_instru), .in1(minst_1_instru), .out(multiplexer_3_out), .sel(minst_1_op));
  MINST minst_1 (.INST(FETCH_OUT), .ADR_SAVE(FETCH_OUT), .INSTRU(minst_1_instru), .OP(minst_1_op));
  Multiplexer #(.width(16), .enable("false")) multiplexer_4 (
    .in0(FETCH_OUT), .in1(multiplexer_3_out), .out(multiplexer_4_out), .sel(or_1_out));
  or or_1 (or_1_out, binst_1_op, minst_1_op);
  // Probe on multiplexer_4_out

  // Notes on the sheet:
  //   LABO ARO 2 - FETCH
  //   HEIG-VD / Institut REDS
  //   Date : 25.02.2014
  //   Ne pas modifier les noms des clocks
  //   contents of MEM_INSTRU (hex, n*v repeats v):
  //   2103 188b e7fc 21*0 18d1 2302 1c2c
endmodule

module FETCH_16BITS (
  input  clk,
  input  CLR,
  output [14:0] PC_IN,
  output [15:0] FETCH_OUT
);

  wire [0:0] PC_q;
  wire [15:0] adder_1_out;

  // Text text_1: pin names not known
  // Text text_2: pin names not known
  // Text text_3: pin names not known
  // Text text_4: pin names not known
  // Text text_5: pin names not known
  Adder #(.width(16)) adder_1 (.a({PC_IN, PC_q[0]}), .b(16'h2), .out(adder_1_out));  // open: cin, cout
  Register #(.width(16)) PC (.D(adder_1_out), .en(1'b1), .clk(clk), .Q({PC_IN, PC_q[0]}), .clr(CLR));
  ROM #(.addrWidth(15), .dataWidth(16)) MEM_INSTRU (.addr(PC_IN), .data(FETCH_OUT));

  // Notes on the sheet:
  //   contents of MEM_INSTRU (hex, n*v repeats v):
  //   2103 188b 18cc 2502
endmodule

module FETCH_JUMP_16BITS (
  input  JUMP,
  input  clk,
  input  CLR,
  output [14:0] PC_IN,
  output [15:0] FETCH_OUT
);

  wire binst_1_op;
  wire [0:0] PC_q;
  wire [15:0] adder_1_out, binst_1_instru, calc_adr_1_adr_out, multiplexer_1_out, multiplexer_2_out,
       multiplexer_3_out, multiplier_1_out;

  // Text text_1: pin names not known
  // Text text_2: pin names not known
  // Text text_3: pin names not known
  // Text text_4: pin names not known
  // Text text_5: pin names not known
  Adder #(.width(16)) adder_1 (.a({PC_IN, PC_q[0]}), .b(16'h2), .out(adder_1_out));  // open: cin, cout
  Multiplier #(.width(16)) multiplier_1 (.a(16'h2), .b(16'h2024), .out(multiplier_1_out));  // open: cin, cout
  Multiplexer #(.width(16), .enable("false")) multiplexer_1 (
    .in0(adder_1_out), .in1(multiplier_1_out), .out(multiplexer_1_out), .sel(JUMP));
  // Probe on calc_adr_1_adr_out
  CALC_ADR calc_adr_1 (.PC({PC_IN, PC_q[0]}), .ADR(multiplexer_3_out), .ADR_OUT(calc_adr_1_adr_out));
  Multiplexer #(.width(16), .enable("false")) multiplexer_2 (
    .in0(multiplexer_1_out), .in1(calc_adr_1_adr_out), .out(multiplexer_2_out), .sel(binst_1_op));
  Register #(.width(16)) PC (.D(multiplexer_2_out), .en(1'b1), .clk(clk), .Q({PC_IN, PC_q[0]}), .clr(CLR));
  ROM #(.addrWidth(15), .dataWidth(16)) MEM_INSTRU (.addr(PC_IN), .data(FETCH_OUT));
  BINST binst_1 (.INST(FETCH_OUT), .INSTRU(binst_1_instru), .OP(binst_1_op));
  Multiplexer #(.width(16), .enable("false")) multiplexer_3 (
    .in0(FETCH_OUT), .in1(binst_1_instru), .out(multiplexer_3_out), .sel(binst_1_op));
  // Probe on multiplexer_3_out

  // Notes on the sheet:
  //   contents of MEM_INSTRU (hex, n*v repeats v):
  //   2103 188b e7fc 21*0 18cc 2502 1c2c
endmodule

module BINST (
  input  [15:0] INST,
  output [15:0] INSTRU,
  output OP
);

  wire not_1_out, not_2_out;

  // Text text_1: pin names not known
  // Text text_2: pin names not known
  // Text text_3: pin names not known
  // Text text_4: pin names not known
  // Text text_5: pin names not known
  not not_1 (not_1_out, INST[11]);
  not not_2 (not_2_out, INST[12]);
  assign INSTRU = {{5{INST[10]}}, INST[10:0]};  // Bit_Extender bit_extender_1
  and and_1 (OP, not_1_out, not_2_out, INST[13], INST[14], INST[15]);
endmodule

module CALC_ADR (
  input  [15:0] PC,
  input  [15:0] ADR,
  output [15:0] ADR_OUT
);

  wire [15:0] adder_1_out, multiplier_1_out;

  // Text text_1: pin names not known
  // Text text_2: pin names not known
  // Text text_3: pin names not known
  // Text text_4: pin names not known
  // Text text_5: pin names not known
  Multiplier #(.width(16)) multiplier_1 (.a(16'h2), .b(ADR), .out(multiplier_1_out));  // open: cin, cout
  Adder #(.width(16)) adder_1 (.a(PC), .b(multiplier_1_out), .out(adder_1_out));  // open: cin, cout
  Adder #(.width(16)) adder_2 (.a(16'h4), .b(adder_1_out), .out(ADR_OUT));  // open: cin, cout
endmodule

module MINST (
  input  [15:0] INST,
  input  [15:0] ADR_SAVE,
  output [15:0] INSTRU,
  output OP
);

  wire nand_1_out, nand_2_out, not_1_out;

  // Text text_1: pin names not known
  // Text text_2: pin names not known
  // Text text_3: pin names not known
  // Text text_4: pin names not known
  // Text text_5: pin names not known; wires that end beside it: ADR_SAVE
  not not_1 (not_1_out, INST[9]);
  nand nand_1 (nand_1_out, INST[6], INST[7], INST[8]);
  nand nand_2 (nand_2_out, INST[13], INST[14], INST[15]);
  Bit_Extender #(.in_width(6), .\type ("zero")) bit_extender_1 (.out(INSTRU));  // open: in
  and and_1 (OP, nand_1_out, not_1_out, INST[10], INST[11], INST[12], nand_2_out);
endmodule
