// Logisim project Labo_decode_v2_Et4.circ as structural Verilog: 9 circuits, main circuit main
module main (
  output [15:0] out_1,
  output [15:0] out_2
);

  wire mainclk, reset_out, Sys_clk;
  wire [0:0] prodis1_1_inst_adr;
  wire [3:0] IRQ1_out;
  wire [14:0] prodis1_1_inst_adr_2;
  wire [15:0] rom_1_data;

  // Text text_1: pin names not known
  // Text text_2: pin names not known
  // Text text_3: pin names not known
  // Text text_4: pin names not known
  // Text text_5: pin names not known
  Button IRQ1 (.out(IRQ1_out[0]));
  Button IRQ2 (.out(IRQ1_out[1]));
  Button IRQ3 (.out(IRQ1_out[2]));
  Button IRQ4 (.out(IRQ1_out[3]));
  Button reset (.out(reset_out));
  Clock #(.highDuration(4), .lowDuration(4)) clk (.out(mainclk));
  Clock sysclk (.out(Sys_clk));
  ROM #(.addrWidth(15), .dataWidth(16)) rom_1 (.addr(prodis1_1_inst_adr_2), .data(rom_1_data));
  prodis1 prodis1_1 (
    .inst_adr({prodis1_1_inst_adr_2, prodis1_1_inst_adr[0]}), .inst_data(rom_1_data), .reset(reset_out),
    .interrupt(IRQ1_out), .clock(mainclk));
  DECODE decode_1 (.INST(rom_1_data), .clk(mainclk), .CLR(reset_out), .S_Rn(out_1), .S_Rm(out_2));

  // Notes on the sheet:
  //   Auteur:
  //   Date:
  //   LABO ARO 2 - DECODE
  //   HEIG-VD - Institut ReDS
  //   Ne pas modifier le nom des clocks
  //   contents of rom_1 (hex, n*v repeats v):
  //   2102 2319 18d1 210c 1888 1c03
endmodule

module prodis1 (
  input  [15:0] inst_data,
  input  [3:0] interrupt,
  input  reset,
  input  clock,
  output [15:0] inst_adr
);

  wire branch, interrupt_en;
  wire [15:0] fetch_1_inst_out, PC_fut, PC_pres;

  // Text text_1: pin names not known
  // Text text_2: pin names not known
  // Text text_3: pin names not known
  // Text text_4: pin names not known
  // Text text_5: pin names not known
  Fetch fetch_1 (
    .jump_adr({16{1'b0}}), .inst_out(fetch_1_inst_out), .inst_data(inst_data), .inst_adr(inst_adr),
    .cpsr({5{1'b0}}), .sel_PC({6{1'b0}}), .IRQ_bus(interrupt), .PC_fut(PC_fut), .PC_pres(PC_pres),
    .interrupt_en(interrupt_en), .branch(branch), .clock(clock), .reset(reset));
  // Probe on fetch_1_inst_out
  Register #(.width(16)) PC (.D(PC_fut), .en(1'b1), .clk(clock), .Q(PC_pres), .clr(reset));

  // Other names for the same wires on the sheet: CLK = clock; RST = reset
endmodule

module Fetch (
  input  [15:0] PC_pres,
  input  [15:0] inst_data,
  input  [15:0] jump_adr,
  input  [3:0] IRQ_bus,
  input  reset,
  input  [5:0] sel_PC,
  input  clock,
  input  [4:0] cpsr,
  output [15:0] inst_adr,
  output [15:0] inst_out,
  output [15:0] PC_fut,
  output interrupt_en,
  output branch
);

  wire test_cond_1_test_cond;
  wire [15:0] adder_1_out, interrupt_adr;

  // Text text_1: pin names not known
  // Text text_2: pin names not known
  // Text text_3: pin names not known
  // Text text_4: pin names not known
  // Text text_5: pin names not known
  Test_cond test_cond_1 (
    .cond(sel_PC[5:2]), .Z(cpsr[0]), .C(cpsr[2]), .N(cpsr[1]), .V(cpsr[3]),
    .test_cond(test_cond_1_test_cond), .cond_en(sel_PC[1]));
  Adder #(.width(16)) adder_1 (.a(PC_pres), .b(16'h2), .out(adder_1_out));  // open: cin, cout
  and and_1 (branch, sel_PC[0], test_cond_1_test_cond);
  Multiplexer #(.select(2), .width(16), .enable("false")) multiplexer_1 (
    .in0(adder_1_out), .in1(jump_adr), .in2(interrupt_adr), .in3(interrupt_adr), .out(PC_fut),
    .sel({interrupt_en, branch}));
  Gestion_Interruption gestion_interruption_1 (
    .IRQ4(IRQ_bus[3]), .IRQ3(IRQ_bus[2]), .interrupt_en(interrupt_en), .IRQ2(IRQ_bus[1]), .IRQ1(IRQ_bus[0]),
    .clock(clock), .I_flag(cpsr[4]), .interrupt_adr(interrupt_adr), .reset(reset));

  assign inst_adr = PC_pres;
  assign inst_out = inst_data;

  // Other names for the same wires on the sheet: I_flag = cpsr[4]

  // Notes on the sheet:
  //   FETCH v1.1
  //   Ce bloc test si la condition requise par l'instruction est correcte.
  //   Cela n'est utile que pour les branch en Thumb code.
  //   la valeur actuelle du PC, soit en sélectionnant une adresse de saut.
  //   Ce bloc s'occupe d'envoyer la bonne adresse à la mémoire d'instruction, soit en incrémentant
  //   Le bloc reçoit en retour l'instruction stockée dans la mémoire, qu'il va en ensuite envoyer au bloc suivant : Le décodage.
  //   Incrémentation du PC 
endmodule

module Test_cond (
  input  cond_en,
  input  [3:0] cond,
  input  Z,
  input  C,
  input  N,
  input  V,
  output test_cond
);

  wire and_1_out, and_2_out, comparator_1_eq, not_1_out, not_2_out, not_3_out, not_4_out, not_5_out,
       not_6_out, not_7_out, not_8_out, or_1_out, or_2_out;
  wire [3:0] multiplexer_1_out;

  // Text text_1: pin names not known
  // Text text_2: pin names not known
  // Text text_3: pin names not known
  // Text text_4: pin names not known
  // Text text_5: pin names not known
  and and_1 (and_1_out, C, not_1_out);
  not not_1 (not_1_out, Z);
  not not_2 (not_2_out, C);
  or or_1 (or_1_out, not_2_out, Z);
  Comparator #(.width(1), .mode("unsigned")) comparator_1 (.a(N), .b(V), .eq(comparator_1_eq));  // open: gt, lt
  not not_3 (not_3_out, Z);
  not not_4 (not_4_out, comparator_1_eq);
  and and_2 (and_2_out, comparator_1_eq, not_3_out);
  or or_2 (or_2_out, not_4_out, Z);
  not not_5 (not_5_out, Z);
  not not_6 (not_6_out, C);
  not not_7 (not_7_out, N);
  not not_8 (not_8_out, V);
  Multiplexer #(.width(4), .enable("false")) multiplexer_1 (
    .in0(4'b1110), .in1(cond), .out(multiplexer_1_out), .sel(cond_en));
  Multiplexer #(.select(4), .enable("false")) multiplexer_2 (
    .in0(Z), .in1(not_5_out), .in2(C), .in3(not_6_out), .in4(N), .in5(not_7_out), .in6(V), .in7(not_8_out),
    .in8(and_1_out), .in9(or_1_out), .in10(comparator_1_eq), .in11(not_4_out), .in12(and_2_out),
    .in13(or_2_out), .in14(1'b1), .in15(1'b1), .out(test_cond), .sel(multiplexer_1_out));

  // Notes on the sheet:
  //   TEST COND v1.0
  //   sélectionnera le bon test.
  //   Ce bloc reçoit les valeurs actuels des flags de conditions, et, suivant l'instruction conditionnelle,
  //   Si l'instruction n'est pas conditionnelle, alors on choisis la "condition" always, qui est toujours à 1.
  //   Always (Inconditionnel)
endmodule

module Gestion_Interruption (
  input  IRQ4,
  input  IRQ3,
  input  IRQ2,
  input  IRQ1,
  input  clock,
  input  I_flag,
  input  reset,
  output interrupt_en,
  output [15:0] interrupt_adr
);

  wire rst, s_r_ff_1_q, s_r_ff_2_q, s_r_ff_3_q, s_r_ff_4_q;
  wire [1:0] priority_encoder_1_out;

  // Text text_1: pin names not known
  // Text text_2: pin names not known
  // Text text_3: pin names not known
  // Text text_4: pin names not known
  // Text text_5: pin names not known
  S_R_Flip_Flop s_r_ff_1 (.S(IRQ4), .R(1'b0), .clk(clock), .Q(s_r_ff_1_q), .reset(rst));  // open: Qn, preset
  S_R_Flip_Flop s_r_ff_2 (.S(IRQ3), .R(1'b0), .clk(clock), .Q(s_r_ff_2_q), .reset(rst));  // open: Qn, preset
  S_R_Flip_Flop s_r_ff_3 (.S(IRQ2), .R(1'b0), .clk(clock), .Q(s_r_ff_3_q), .reset(rst));  // open: Qn, preset
  S_R_Flip_Flop s_r_ff_4 (.S(IRQ1), .R(1'b0), .clk(clock), .Q(s_r_ff_4_q), .reset(rst));  // open: Qn, preset
  or or_1 (rst, I_flag, reset);
  Priority_Encoder #(.select(2)) priority_encoder_1 (
    .in0(s_r_ff_4_q), .in1(s_r_ff_3_q), .in2(s_r_ff_2_q), .in3(s_r_ff_1_q), .out(priority_encoder_1_out));  // open: gs, en_out, en_in
  or or_2 (interrupt_en, s_r_ff_1_q, s_r_ff_2_q, s_r_ff_3_q, s_r_ff_4_q);
  Multiplexer #(.select(2), .width(16), .enable("false")) multiplexer_1 (
    .in0(16'he000), .in1(16'he200), .in2(16'he400), .in3(16'he600), .out(interrupt_adr),
    .sel(priority_encoder_1_out));

  // Other names for the same wires on the sheet: clk = clock

  // Notes on the sheet:
  //   INTERRUPT UNIT v1.0
  //   4 interruptions sont pour l'instant en place. Les sauts vont aux adresses suivantes en fonction de l'IRQ :
  //   IRQ 1 : 0xE000
  //   IRQ 2 : 0xE200
  //   IRQ 3 : 0xE400
  //   IRQ 4 : 0xE600
endmodule

module REGISTERS_16BITS (
  input  [15:0] W_DATA,
  input  RnInRd,
  input  [1:0] Rn,
  input  [1:0] Rm,
  input  WRITE_EN,
  input  [1:0] Rd,
  input  clk,
  input  CLR,
  output [15:0] OUT_DATA_Rn,
  output [15:0] OUT_DATA_Rm
);

  wire decoder_1_out0, decoder_1_out1, decoder_1_out2, decoder_1_out3;
  wire [15:0] adder_1_out, multiplexer_1_out, R0_q, R1_q, R2_q, R3_q;

  // Text text_1: pin names not known
  // Text text_2: pin names not known
  // Text text_3: pin names not known
  // Text text_4: pin names not known
  // Text text_5: pin names not known
  Multiplexer #(.width(16), .enable("false")) multiplexer_1 (
    .in0(W_DATA), .in1(adder_1_out), .out(multiplexer_1_out), .sel(RnInRd));
  Decoder #(.select(2)) decoder_1 (
    .out0(decoder_1_out0), .out1(decoder_1_out1), .out2(decoder_1_out2), .out3(decoder_1_out3), .sel(Rd),
    .en(WRITE_EN));
  Register #(.width(16)) R0 (.D(multiplexer_1_out), .en(decoder_1_out0), .clk(clk), .Q(R0_q), .clr(CLR));
  Register #(.width(16)) R1 (.D(multiplexer_1_out), .en(decoder_1_out1), .clk(clk), .Q(R1_q), .clr(CLR));
  Register #(.width(16)) R2 (.D(multiplexer_1_out), .en(decoder_1_out2), .clk(clk), .Q(R2_q), .clr(CLR));
  Register #(.width(16)) R3 (.D(multiplexer_1_out), .en(decoder_1_out3), .clk(clk), .Q(R3_q), .clr(CLR));
  Multiplexer #(.select(2), .width(16), .enable("false")) multiplexer_2 (
    .in0(R0_q), .in1(R1_q), .in2(R2_q), .in3(R3_q), .out(OUT_DATA_Rn), .sel(Rn));
  Multiplexer #(.select(2), .width(16), .enable("false")) multiplexer_3 (
    .in0(R0_q), .in1(R1_q), .in2(R2_q), .in3(R3_q), .out(OUT_DATA_Rm), .sel(Rm));
  Adder #(.width(16)) adder_1 (.a(OUT_DATA_Rn), .b(OUT_DATA_Rm), .out(adder_1_out));  // open: cin, cout
endmodule

module MOV_INST (
  input  [15:0] INST,
  output [1:0] Rd,
  output [1:0] Rn,
  output [7:0] Imm,
  output [1:0] Rd_Imm,
  output IsMov,
  output IsMovImm
);

  wire comparator_2_eq;

  // Text text_1: pin names not known
  // Text text_2: pin names not known
  // Text text_3: pin names not known
  // Text text_4: pin names not known
  // Text text_5: pin names not known
  Comparator #(.width(5)) comparator_1 (.a(INST[15:11]), .b(5'b00100), .eq(IsMovImm));  // open: gt, lt
  Comparator #(.width(10)) comparator_2 (.a(INST[15:6]), .b(10'h70), .eq(comparator_2_eq));  // open: gt, lt
  or or_1 (IsMov, comparator_2_eq, IsMovImm);

  assign Imm = INST[7:0];
  assign Rd = INST[1:0];
  assign Rd_Imm = INST[9:8];
  assign Rn = INST[4:3];
endmodule

module DECODE (
  input  [15:0] INST,
  input  clk,
  input  CLR,
  output [15:0] S_Rn,
  output [15:0] S_Rm
);

  wire add_inst_1_isadd, add_inst_1_isimm, mov_inst_1_ismov, mov_inst_1_ismovimm, not_1_out, or_1_out;
  wire [1:0] add_inst_1_rd, add_inst_1_rm, add_inst_1_rn, demultiplexer_1_out0, demultiplexer_1_out1,
       mov_inst_1_rd, mov_inst_1_rd_imm, mov_inst_1_rn, multiplexer_1_out, multiplexer_2_out,
       multiplexer_3_out;
  wire [7:0] mov_inst_1_imm;
  wire [15:0] bit_extender_1_out, bit_extender_2_out, multiplexer_4_out;

  // Text text_1: pin names not known
  // Text text_2: pin names not known
  // Text text_3: pin names not known
  // Text text_4: pin names not known
  // Text text_5: pin names not known
  MOV_INST mov_inst_1 (
    .INST(INST), .Rd(mov_inst_1_rd), .Rn(mov_inst_1_rn), .Imm(mov_inst_1_imm), .Rd_Imm(mov_inst_1_rd_imm),
    .IsMov(mov_inst_1_ismov), .IsMovImm(mov_inst_1_ismovimm));
  ADD_INST add_inst_1 (
    .INST(INST), .Rd(add_inst_1_rd), .Rn(add_inst_1_rn), .Rm(add_inst_1_rm), .IsAdd(add_inst_1_isadd),
    .IsImm(add_inst_1_isimm));
  assign bit_extender_1_out = {{8{1'b0}}, mov_inst_1_imm};  // Bit_Extender bit_extender_1
  Multiplexer #(.width(2), .enable("false")) multiplexer_1 (
    .in0(mov_inst_1_rd), .in1(mov_inst_1_rd_imm), .out(multiplexer_1_out), .sel(mov_inst_1_ismovimm));
  Demultiplexer #(.width(2), .enable("false")) demultiplexer_1 (
    .out0(demultiplexer_1_out0), .out1(demultiplexer_1_out1), .in(add_inst_1_rm), .sel(add_inst_1_isimm));
  Multiplexer #(.width(2), .enable("false")) multiplexer_2 (
    .in0(multiplexer_1_out), .in1(add_inst_1_rd), .out(multiplexer_2_out), .sel(add_inst_1_isadd));
  assign bit_extender_2_out = {{14{1'b0}}, demultiplexer_1_out0};  // Bit_Extender bit_extender_2
  Multiplexer #(.width(2), .enable("false")) multiplexer_3 (
    .in0(mov_inst_1_rn), .in1(add_inst_1_rn), .out(multiplexer_3_out), .sel(add_inst_1_isadd));
  // Probe on multiplexer_3_out
  Multiplexer #(.width(16), .enable("false")) multiplexer_4 (
    .in0(bit_extender_1_out), .in1(bit_extender_2_out), .out(multiplexer_4_out), .sel(add_inst_1_isadd));
  // Probe on multiplexer_4_out
  // Probe on demultiplexer_1_out1
  not not_1 (not_1_out, mov_inst_1_ismovimm);
  or or_1 (or_1_out, mov_inst_1_ismov, add_inst_1_isadd);
  // Probe on multiplexer_2_out
  REGISTERS_16BITS registers_16bits_1 (
    .W_DATA(multiplexer_4_out), .RnInRd(not_1_out), .Rn(multiplexer_3_out), .Rm(demultiplexer_1_out1),
    .WRITE_EN(or_1_out), .Rd(multiplexer_2_out), .clk(clk), .CLR(CLR), .OUT_DATA_Rn(S_Rn), .OUT_DATA_Rm(S_Rm));
endmodule

module ADD_INST (
  input  [15:0] INST,
  output [1:0] Rd,
  output [1:0] Rn,
  output [1:0] Rm,
  output IsAdd,
  output IsImm
);

  wire and_1_out, and_2_out, comparator_1_eq, comparator_2_eq, multiplexer_1_out, nor_1_out, nor_2_out,
       not_1_out, not_2_out;
  wire [2:0] text_2_p1, text_2_p1_2, text_2_p1_3;
  wire [6:0] text_2_p1_4;

  // Text text_1: pin names not known
  // Text text_2: pin names not known; wires that end beside it: {text_2_p1_4, text_2_p1_3, text_2_p1_2, text_2_p1}
  // Text text_3: pin names not known
  // Text text_4: pin names not known
  // Text text_5: pin names not known
  Comparator #(.width(7)) comparator_1 (.a(text_2_p1_4), .b(7'b0001110), .eq(comparator_1_eq));  // open: gt, lt
  Comparator #(.width(7)) comparator_2 (.a(text_2_p1_4), .b(7'b0001100), .eq(comparator_2_eq));  // open: gt, lt
  nor nor_1 (nor_1_out, INST[6], INST[7], INST[8]);
  and and_1 (and_1_out, INST[11], INST[12]);
  Multiplexer #(.enable("false")) multiplexer_1 (
    .in0(comparator_1_eq), .in1(comparator_2_eq), .out(multiplexer_1_out), .sel(comparator_2_eq));
  nor nor_2 (nor_2_out, INST[13], INST[14], INST[15]);
  not not_1 (not_1_out, nor_1_out);
  not not_2 (not_2_out, INST[9]);
  and and_2 (and_2_out, not_2_out, and_1_out, nor_2_out);
  and and_3 (IsAdd, not_1_out, and_2_out);

  assign IsImm = INST[10];
  assign Rd = INST[1:0];
  assign Rm = INST[7:6];
  assign Rn = INST[4:3];
endmodule
