// Logisim project Template.circ as structural Verilog: 6 circuits, main circuit main
module main (
  input  CLR,
  output [14:0] PC_IN,
  output [15:0] FETCH_OUT,
  output [2:0] Rd,
  output [2:0] Rn
);

  wire branch_inst_1_op, clk, INTER_out, mov_inst_1_op, or_1_out;
  wire [0:0] PC_q;
  wire [15:0] adder_1_out, adder_2_out, branch_inst_1_inst_out, calc_adr_1_adr_out, LR_q, multiplexer_1_out,
       multiplexer_2_out, multiplexer_3_out, multiplexer_4_out;

  // Text text_1: pin names not known
  // Text text_2: pin names not known
  // Text text_3: pin names not known
  // Text text_4: pin names not known
  // Text text_5: pin names not known; wires that end beside it: CLR
  Adder #(.width(16)) adder_1 (.a({PC_IN, PC_q[0]}), .b(16'h2), .out(adder_1_out));  // open: cin, cout
  Button INTER (.out(INTER_out));
  Multiplexer #(.width(16), .enable("false")) multiplexer_1 (
    .in0(adder_1_out), .in1(16'h30), .out(multiplexer_1_out), .sel(INTER_out));
  Clock #(.highDuration(4), .lowDuration(4)) u_clk (.out(clk));
  Clock sysclk ();  // open: out
  Multiplexer #(.width(16), .enable("false")) multiplexer_2 (
    .in0(multiplexer_1_out), .in1(calc_adr_1_adr_out), .out(multiplexer_2_out), .sel(or_1_out));
  // Probe on calc_adr_1_adr_out
  CALC_ADR calc_adr_1 (
    .PC({PC_IN, PC_q[0]}), .ADR(multiplexer_4_out), .COMPUTE(mov_inst_1_op), .ADR_OUT(calc_adr_1_adr_out));
  Register #(.width(16)) PC (.D(multiplexer_2_out), .en(1'b1), .clk(clk), .Q({PC_IN, PC_q[0]}), .clr(CLR));
  ROM #(.addrWidth(15), .dataWidth(16)) MEM_INSTRU (.addr(PC_IN), .data(FETCH_OUT));
  MOV_INST mov_inst_1 (.INST(FETCH_OUT), .Rd(Rd), .Rn(Rn), .OP(mov_inst_1_op));
  Register #(.width(16)) LR (.D({PC_IN, PC_q[0]}), .en(INTER_out), .clk(clk), .Q(LR_q), .clr(CLR));
  BRANCH_INST branch_inst_1 (.INST(FETCH_OUT), .INST_OUT(branch_inst_1_inst_out), .OP(branch_inst_1_op));
  Multiplexer #(.width(16), .enable("false")) multiplexer_3 (
    .in0(branch_inst_1_inst_out), .in1(adder_2_out), .out(multiplexer_3_out), .sel(mov_inst_1_op));
  Adder #(.width(16)) adder_2 (.a(16'h2), .b(LR_q), .out(adder_2_out));  // open: cin, cout
  Multiplexer #(.width(16), .enable("false")) multiplexer_4 (
    .in0(FETCH_OUT), .in1(multiplexer_3_out), .out(multiplexer_4_out), .sel(or_1_out));
  or or_1 (or_1_out, branch_inst_1_op, mov_inst_1_op);
  // Probe on multiplexer_4_out

  // Notes on the sheet:
  //   LABO ARO 2 - FETCH
  //   HEIG-VD / Institut REDS
  //   Date : 25.02.2014
  //   Ne pas modifier les noms des clocks
  //   contents of MEM_INSTRU (hex, n*v repeats v):
  //   2103 188b 189c 3404 e7fa 19*0 18d1 2104 2302 1c2c
endmodule

module FETCH_16BITS (
  input  clk,
  input  CLR,
  output [14:0] PC_IN,
  output [15:0] FETCH_OUT
);

  wire [0:0] PC_q;
  wire [15:0] adder_1_out;

  // Text text_1: pin names not known
  // Text text_2: pin names not known
  // Text text_3: pin names not known
  // Text text_4: pin names not known
  // Text text_5: pin names not known
  Adder #(.width(16)) adder_1 (.a({PC_IN, PC_q[0]}), .b(16'h2), .out(adder_1_out));  // open: cin, cout
  Register #(.width(16)) PC (.D(adder_1_out), .en(1'b1), .clk(clk), .Q({PC_IN, PC_q[0]}), .clr(CLR));
  ROM #(.addrWidth(15), .dataWidth(16)) MEM_INSTRU (.addr(PC_IN), .data(FETCH_OUT));

  // Notes on the sheet:
  //   contents of MEM_INSTRU (hex, n*v repeats v):
  //   2103 188b 189c 3404 e7fa 19*0 18d1 2104 2302 1c2c
endmodule

module FETCH_JUMP_16BITS (
  input  JUMP,
  input  clk,
  input  CLR,
  output [14:0] PC_IN,
  output [15:0] FETCH_OUT
);

  wire branch_inst_1_op;
  wire [0:0] calc_adr_1_p1;
  wire [15:0] adder_1_out, branch_inst_1_inst_out, calc_adr_1_p2, calc_adr_1_p3, multiplexer_1_out,
       multiplexer_2_out, multiplier_1_out;

  // Text text_1: pin names not known
  // Text text_2: pin names not known
  // Text text_3: pin names not known
  // Text text_4: pin names not known
  // Text text_5: pin names not known
  Adder #(.width(16)) adder_1 (.a({PC_IN, calc_adr_1_p1[0]}), .b(16'h2), .out(adder_1_out));  // open: cin, cout
  Multiplier #(.width(16)) multiplier_1 (.a(16'h2), .b(16'h30), .out(multiplier_1_out));  // open: cin, cout
  Multiplexer #(.width(16), .enable("false")) multiplexer_1 (
    .in0(adder_1_out), .in1(multiplier_1_out), .out(multiplexer_1_out), .sel(JUMP));
  // Probe on calc_adr_1_p3
  // CALC_ADR calc_adr_1: pin names not known; wires that end beside it: {PC_IN, calc_adr_1_p1[0]}, calc_adr_1_p2, calc_adr_1_p3
  Multiplexer #(.width(16), .enable("false")) multiplexer_2 (
    .in0(multiplexer_1_out), .in1(calc_adr_1_p3), .out(multiplexer_2_out), .sel(branch_inst_1_op));
  Register #(.width(16)) PC (.D(multiplexer_2_out), .en(1'b1), .clk(clk), .Q({PC_IN, calc_adr_1_p1[0]}), .clr(CLR));
  ROM #(.addrWidth(15), .dataWidth(16)) MEM_INSTRU (.addr(PC_IN), .data(FETCH_OUT));
  BRANCH_INST branch_inst_1 (.INST(FETCH_OUT), .INST_OUT(branch_inst_1_inst_out), .OP(branch_inst_1_op));
  Multiplexer #(.width(16), .enable("false")) multiplexer_3 (
    .in0(FETCH_OUT), .in1(branch_inst_1_inst_out), .out(calc_adr_1_p2), .sel(branch_inst_1_op));
  // Probe on calc_adr_1_p2

  // Notes on the sheet:
  //   contents of MEM_INSTRU (hex, n*v repeats v):
  //   2103 188b e7fc 21*0 18cc 2502 1c2c
endmodule

module BRANCH_INST (
  input  [15:0] INST,
  output [15:0] INST_OUT,
  output OP
);

  // Text text_1: pin names not known
  // Text text_2: pin names not known
  // Text text_3: pin names not known
  // Text text_4: pin names not known
  // Text text_5: pin names not known
  assign INST_OUT = {{5{INST[10]}}, INST[10:0]};  // Bit_Extender bit_extender_1
  Comparator #(.width(5)) comparator_1 (.a(INST[15:11]), .b(5'b11100), .eq(OP));  // open: gt, lt
endmodule

module CALC_ADR (
  input  [15:0] PC,
  input  [15:0] ADR,
  input  COMPUTE,
  output [15:0] ADR_OUT
);

  wire [15:0] adder_1_out, adder_2_out, multiplier_1_out;

  // Text text_1: pin names not known
  // Text text_2: pin names not known
  // Text text_3: pin names not known
  // Text text_4: pin names not known
  // Text text_5: pin names not known
  Multiplier #(.width(16)) multiplier_1 (.a(16'h2), .b(ADR), .out(multiplier_1_out));  // open: cin, cout
  Adder #(.width(16)) adder_1 (.a(PC), .b(multiplier_1_out), .out(adder_1_out));  // open: cin, cout
  Adder #(.width(16)) adder_2 (.a(16'h4), .b(adder_1_out), .out(adder_2_out));  // open: cin, cout
  Multiplexer #(.width(16), .enable("false")) multiplexer_1 (
    .in0(adder_2_out), .in1(ADR), .out(ADR_OUT), .sel(COMPUTE));
endmodule

module MOV_INST (
  input  [15:0] INST,
  output [2:0] Rd,
  output [2:0] Rn,
  output OP
);

  // Text text_1: pin names not known
  // Text text_2: pin names not known
  // Text text_3: pin names not known
  // Text text_4: pin names not known
  // Text text_5: pin names not known
  Comparator #(.width(10)) comparator_1 (.a(INST[15:6]), .b(10'h70), .eq(OP));  // open: gt, lt

  assign Rd = INST[2:0];
  assign Rn = INST[5:3];
endmodule
